# Fritzing sketch Photobooth (saved by Fritzing 0.8.7b)
breadboards: 1

parts:
  U1 = TLP621 [package=THT]
  R1 = Resistor [tolerance=±5% resistance=220 package=THT]
  Gertduino = Arduino Uno (Rev3)
  USB_E-510 = USB Connectors [package=usb-a-s-silk-female]
  JP1 = RCA [package=rca_lock]  # not connected
  JP2 = Header 12 [package=1x12_machine-pin-header_lock.004]
  SG1 = Buzzer 12mm [package=buzzer-12mm-ns-kit]  # not connected
  7_Segment1 = 7 Segment Display  # not connected
  8x8_LED = LED Matrix - Serial Interface - Red/Green/Blue  # not connected
  Raspberry_Pi_B_rev1 = Raspberry Pi B rev2  # not connected
  K1 = Relay [part_number=FRS1B-S package=THT]

nets:
  N1: U1.Pin_1, R1.Pin_1
  N2: U1.Pin_2, Gertduino.GND, K1.COIL1
  N3: U1.Pin_4, JP2.1
  N4: U1.Pin_3, JP2.2, JP2.3
  N5: R1.Pin_0, Gertduino.D2
  N6: Gertduino.D3_PWM, K1.COIL2
  N7: USB_E-510.VBUS, K1.B
  N8: K1.C1, K1.C2

notes:
  E-510
